// Logisim project cpu-circuit.circ as structural Verilog: 1 circuit, main circuit main
module main (
);

  wire and_1_out, and_3_out, CARR_BIT, CARRY_FLAG, CLK, clock_1_out, COUNT_ENABLE, DISP_REG_WRITE, EO,
       FLAG_REG_WRITE, JUMP, MEM_READ, MEM_WRITE, n7_segment_display_1_p1, n7_segment_display_2_p1,
       n7_segment_display_3_p1, n7_segment_display_4_p1, n7_segment_display_5_p1, n7_segment_display_6_p1,
       n7_segment_display_7_p1, n7_segment_display_8_p1, n7_segment_display_9_p1, n7_segment_display_10_p1,
       n7_segment_display_11_p1, n7_segment_display_12_p1, not_1_out, not_2_out, not_3_out, not_4_out,
       not_5_out, not_6_out, PRG_CNT_READ, REG_A_READ, REG_A_WRITE, REG_B_WRITE, REG_INS_READ, REG_INS_WRITE,
       REG_MEMADDR_WRITE, STOP, SUB, undriven, ZERO_FLAG;
  wire [1:0] controlled_buffer_10_out;
  wire [3:0] buffer_10_out, controlled_buffer_9_out, controlled_buffer_11_out, INS_DECODER,
       INSTR_STEP_COUNTER_q;
  wire [7:0] and_2_out, binary_to_bcd_converter_4_p1, buffer_1_out, counter_1_q;
  wire [7:2] register_1_q;
  wire [9:0] dipswitch_2_sw10;
  wire [11:0] INSTR_REG_q;
  wire [15:0] ALU_IN_A, ALU_IN_B, ALU_VALUE, buffer_2_out, BUS_1, controlled_inverter_1_out,
       dipswitch_1_sw16, DISP_REG_q, MEM_ADDRESS_REG_q, ram_1_dout;

  Clock clock_1 (.out(clock_1_out));
  not not_1 (not_1_out, STOP);
  assign CLK = not_1_out ? clock_1_out : 1'bz;  // Controlled_Buffer controlled_buffer_1
  DipSwitch #(.number(16)) dipswitch_1 (
    .sw1(dipswitch_1_sw16[15]), .sw2(dipswitch_1_sw16[14]), .sw3(dipswitch_1_sw16[13]),
    .sw4(dipswitch_1_sw16[12]), .sw5(dipswitch_1_sw16[11]), .sw6(dipswitch_1_sw16[10]),
    .sw7(dipswitch_1_sw16[9]), .sw8(dipswitch_1_sw16[8]), .sw9(dipswitch_1_sw16[7]),
    .sw10(dipswitch_1_sw16[6]), .sw11(dipswitch_1_sw16[5]), .sw12(dipswitch_1_sw16[4]),
    .sw13(dipswitch_1_sw16[3]), .sw14(dipswitch_1_sw16[2]), .sw15(dipswitch_1_sw16[1]),
    .sw16(dipswitch_1_sw16[0]));
  // Probe on dipswitch_1_sw16
  // XOR_Gate xor_1 has open pins: in0=undriven, out=open
  // XOR_Gate xor_2 has open pins: in0=undriven, out=open
  // XOR_Gate xor_3 has open pins: in0=undriven, out=open
  // XOR_Gate xor_4 has open pins: in0=undriven, out=open
  // XOR_Gate xor_5 has open pins: in0=undriven, out=open
  // XOR_Gate xor_6 has open pins: in0=undriven, out=open
  // XOR_Gate xor_7 has open pins: in0=undriven, out=open
  // XOR_Gate xor_8 has open pins: in0=undriven, out=open
  // _7_Segment_Display 7_segment_display_1: pin names not known; wires that end beside it: n7_segment_display_1_p1, n7_segment_display_1_p1
  // BCD_to_7_Segment_decoder bcd_to_7_segment_decoder_1: pin names not known
  // Binary_to_BCD_converter #(.binvalue(8)) binary_to_bcd_converter_1: pin names not known; wires that end beside it: dipswitch_1_sw16[15:8]
  Register #(.width(16)) A_Reg (.D(BUS_1), .en(REG_A_WRITE), .clk(CLK), .Q(ALU_IN_A));  // open: clr
  // _7_Segment_Display 7_segment_display_2: pin names not known; wires that end beside it: n7_segment_display_2_p1, n7_segment_display_2_p1
  // _7_Segment_Display 7_segment_display_3: pin names not known; wires that end beside it: n7_segment_display_3_p1, n7_segment_display_3_p1
  // BCD_to_7_Segment_decoder bcd_to_7_segment_decoder_2: pin names not known
  // BCD_to_7_Segment_decoder bcd_to_7_segment_decoder_3: pin names not known
  not not_2 (not_2_out, REG_A_WRITE);
  and and_1 (and_1_out, not_2_out, REG_A_READ);
  assign BUS_1 = and_1_out ? ALU_IN_A : 16'bz;  // Controlled_Buffer controlled_buffer_2
  // Probe on ALU_IN_A
  Counter counter_1 (
    .load(JUMP), .count(COUNT_ENABLE), .clk(CLK), .D(BUS_1[7:0]), .Q(counter_1_q));  // open: clr, up, carry
  // _7_Segment_Display 7_segment_display_4: pin names not known; wires that end beside it: n7_segment_display_4_p1, n7_segment_display_4_p1
  // BCD_to_7_Segment_decoder bcd_to_7_segment_decoder_4: pin names not known
  // Binary_to_BCD_converter #(.binvalue(8)) binary_to_bcd_converter_2: pin names not known; wires that end beside it: dipswitch_1_sw16[7:0]
  // _7_Segment_Display 7_segment_display_5: pin names not known; wires that end beside it: n7_segment_display_5_p1, n7_segment_display_5_p1
  // BCD_to_7_Segment_decoder bcd_to_7_segment_decoder_5: pin names not known
  // _7_Segment_Display 7_segment_display_6: pin names not known; wires that end beside it: n7_segment_display_6_p1, n7_segment_display_6_p1
  // BCD_to_7_Segment_decoder bcd_to_7_segment_decoder_6: pin names not known
  assign controlled_inverter_1_out = SUB ? ~ALU_IN_B : 16'bz;  // Controlled_Inverter controlled_inverter_1
  not not_3 (not_3_out, SUB);
  assign controlled_inverter_1_out = not_3_out ? ALU_IN_B : 16'bz;  // Controlled_Buffer controlled_buffer_3
  assign buffer_1_out = {8{1'b0}};  // Buffer buffer_1, 8 bits wide
  // _7_Segment_Display 7_segment_display_7: pin names not known; wires that end beside it: n7_segment_display_7_p1, n7_segment_display_7_p1
  // BCD_to_7_Segment_decoder bcd_to_7_segment_decoder_7: pin names not known
  // Binary_to_BCD_converter #(.binvalue(8)) binary_to_bcd_converter_3: pin names not known
  Adder #(.width(16)) adder_1 (
    .a(controlled_inverter_1_out), .b(ALU_IN_A), .out(ALU_VALUE), .cin(SUB), .cout(CARR_BIT));
  assign BUS_1 = PRG_CNT_READ ? {buffer_1_out, counter_1_q} : 16'bz;  // Controlled_Buffer controlled_buffer_4
  // _7_Segment_Display 7_segment_display_8: pin names not known; wires that end beside it: n7_segment_display_8_p1, n7_segment_display_8_p1
  // BCD_to_7_Segment_decoder bcd_to_7_segment_decoder_8: pin names not known
  Register #(.width(16)) DISP_REG (.D(BUS_1), .en(DISP_REG_WRITE), .clk(CLK), .Q(DISP_REG_q));  // open: clr
  Register #(.width(16)) B_REG (.D(BUS_1), .en(REG_B_WRITE), .clk(CLK), .Q(ALU_IN_B));  // open: clr
  assign BUS_1 = EO ? ALU_VALUE : 16'bz;  // Controlled_Buffer controlled_buffer_5
  // Probe on BUS_1
  // Probe on BUS_1
  // _7_Segment_Display 7_segment_display_9: pin names not known; wires that end beside it: n7_segment_display_9_p1, n7_segment_display_9_p1
  // BCD_to_7_Segment_decoder bcd_to_7_segment_decoder_9: pin names not known
  // Probe on DISP_REG_q
  // Probe on BUS_1
  not not_4 (not_4_out, REG_B_WRITE);
  Controlled_Buffer #(.width(8)) controlled_buffer_6 (.en(not_4_out));  // open: in, out
  // Probe on ALU_IN_B
  assign buffer_2_out = ALU_VALUE;  // Buffer buffer_2, 16 bits wide
  and and_2 (and_2_out[0], ~buffer_2_out[0], ~buffer_2_out[1], ~buffer_2_out[2], ~buffer_2_out[3], ~buffer_2_out[4], ~buffer_2_out[5], ~buffer_2_out[6], ~buffer_2_out[7], ~buffer_2_out[8], ~buffer_2_out[9], ~buffer_2_out[10], ~buffer_2_out[11], ~buffer_2_out[12], ~buffer_2_out[13], ~buffer_2_out[14], ~buffer_2_out[15]);  // AND_Gate
  // Buffer buffer_3 is placed but not wired
  buf buffer_4 (and_2_out[2], 1'b0);
  buf buffer_5 (and_2_out[3], 1'b0);
  buf buffer_6 (and_2_out[4], 1'b0);
  buf buffer_7 (and_2_out[5], 1'b0);
  Register register_1 (
    .D({and_2_out[7:2], CARR_BIT, and_2_out[0]}), .en(FLAG_REG_WRITE), .clk(CLK),
    .Q({register_1_q, CARRY_FLAG, ZERO_FLAG}));  // open: clr
  buf buffer_8 (and_2_out[6], 1'b0);
  buf buffer_9 (and_2_out[7], 1'b0);
  LED led_1 (.in(binary_to_bcd_converter_4_p1[7]));
  LED led_2 (.in(binary_to_bcd_converter_4_p1[6]));
  LED led_3 (.in(binary_to_bcd_converter_4_p1[5]));
  // _7_Segment_Display 7_segment_display_10: pin names not known; wires that end beside it: n7_segment_display_10_p1, n7_segment_display_10_p1
  // BCD_to_7_Segment_decoder bcd_to_7_segment_decoder_10: pin names not known
  // Binary_to_BCD_converter #(.binvalue(8)) binary_to_bcd_converter_4: pin names not known; wires that end beside it: binary_to_bcd_converter_4_p1
  Register #(.width(16)) MEM_ADDRESS_REG (
    .D(BUS_1), .en(REG_MEMADDR_WRITE), .clk(CLK), .Q(MEM_ADDRESS_REG_q));  // open: clr
  LED led_4 (.in(binary_to_bcd_converter_4_p1[4]));
  LED led_5 (.in(binary_to_bcd_converter_4_p1[3]));
  LED led_6 (.in(binary_to_bcd_converter_4_p1[2]));
  LED led_7 (.in(binary_to_bcd_converter_4_p1[1]));
  // _7_Segment_Display 7_segment_display_11: pin names not known; wires that end beside it: n7_segment_display_11_p1, n7_segment_display_11_p1
  // _7_Segment_Display 7_segment_display_12: pin names not known; wires that end beside it: n7_segment_display_12_p1, n7_segment_display_12_p1
  // BCD_to_7_Segment_decoder bcd_to_7_segment_decoder_11: pin names not known
  // BCD_to_7_Segment_decoder bcd_to_7_segment_decoder_12: pin names not known
  Register #(.width(16)) INSTR_REG (
    .D(BUS_1), .en(REG_INS_WRITE), .clk(CLK), .Q({INS_DECODER, INSTR_REG_q}));  // open: clr
  // Probe on MEM_ADDRESS_REG_q
  LED led_8 (.in(binary_to_bcd_converter_4_p1[0]));
  // Probe on INSTR_REG_q
  // Probe on {INS_DECODER, INSTR_REG_q}
  // Probe on MEM_ADDRESS_REG_q[7:0]
  not not_5 (not_5_out, REG_INS_WRITE);
  and and_3 (and_3_out, not_5_out, REG_INS_READ);
  assign buffer_10_out = 4'b0000;  // Buffer buffer_10, 4 bits wide
  // Probe on INS_DECODER
  assign BUS_1 = and_3_out ? {buffer_10_out, INSTR_REG_q} : 16'bz;  // Controlled_Buffer controlled_buffer_7
  RAM #(.asyncread("true"), .dataWidth(16), .\type ("nonvolatile")) ram_1 (
    .addr(MEM_ADDRESS_REG_q[7:0]), .we(MEM_WRITE), .clk(CLK), .din(BUS_1), .dout(ram_1_dout));  // open: oe
  Counter #(.max('h4), .width(4)) INSTR_STEP_COUNTER (
    .clk(CLK), .Q(INSTR_STEP_COUNTER_q));  // open: clr, load, up, count, D, carry
  assign BUS_1 = MEM_READ ? ram_1_dout : 16'bz;  // Controlled_Buffer controlled_buffer_8
  // Probe on ram_1_dout
  Decoder #(.enable("false"), .select(4)) decoder_1 (.sel(INSTR_STEP_COUNTER_q));  // open: out0, out1, out2, out3, out4, out5, out6, out7, out8, out9, out10, out11, out12, out13, out14, out15
  DipSwitch #(.number(10)) dipswitch_2 (
    .sw1(dipswitch_2_sw10[9]), .sw2(dipswitch_2_sw10[8]), .sw3(dipswitch_2_sw10[7]),
    .sw4(dipswitch_2_sw10[6]), .sw5(dipswitch_2_sw10[5]), .sw6(dipswitch_2_sw10[4]),
    .sw7(dipswitch_2_sw10[3]), .sw8(dipswitch_2_sw10[2]), .sw9(dipswitch_2_sw10[1]),
    .sw10(dipswitch_2_sw10[0]));
  assign controlled_buffer_9_out = 1'b1 ? INSTR_STEP_COUNTER_q : 4'bz;  // Controlled_Buffer controlled_buffer_9
  assign controlled_buffer_10_out = 1'b1 ? {ZERO_FLAG, CARRY_FLAG} : 2'bz;  // Controlled_Buffer controlled_buffer_10
  assign controlled_buffer_11_out = 1'b1 ? INS_DECODER : 4'bz;  // Controlled_Buffer controlled_buffer_11
  not not_6 (not_6_out, 1'b1);
  // Probe on {controlled_buffer_11_out, controlled_buffer_9_out, controlled_buffer_10_out}
  ROM #(.addrWidth(10), .dataWidth(16)) rom_1 (
    .addr({controlled_buffer_11_out, controlled_buffer_9_out, controlled_buffer_10_out}),
    .data({FLAG_REG_WRITE, REG_A_READ, REG_A_WRITE, REG_B_WRITE, REG_MEMADDR_WRITE, MEM_READ, EO, SUB, REG_INS_WRITE, REG_INS_READ, DISP_REG_WRITE, JUMP, STOP, COUNT_ENABLE, PRG_CNT_READ, MEM_WRITE}));
  assign {controlled_buffer_11_out, controlled_buffer_9_out, controlled_buffer_10_out} = not_6_out ? dipswitch_2_sw10 : 10'bz;  // Controlled_Buffer controlled_buffer_12

  // Other names for the same wires on the sheet: INV_CLK = CLK

  // Notes on the sheet:
  //   DISPLAY / OUTPUT
  //   BUS VALUE
  //   contents of rom_1 (hex, n*v repeats v):
  //   4*802 4*484 56*0 4*802 4*484 4*840 4*2400 48*0 4*802 4*484 4*840 4*1400 48*0 4*802 4*484 4*840
  //   4*1400 4*a200 44*0 4*802 4*484 4*840 4*1400 4*a300 44*0 4*802 4*484 4*4020 52*0 4*802 4*484 4*50
  //   52*0 4*802 4*484 4*840 4*4001 48*0 4*802 4*484 4*2040 52*0 4*802 4*484 0 0 50 50 52*0 4*802 4*484 0
  //   50 0 50 52*0 4*802 4*484 4*8 52*0 4*802 4*484 56*0 4*802 4*484 56*0 4*802 4*484 56*0 4*802 4*484
endmodule
